# Fritzing sketch uart_wiring (saved by Fritzing 0.9.8b)

parts:
  Gizwits_WiFi_Witty_ESP-12F1 = Gizwits WiFi Witty ESP-12F
  Gizwits_WiFi_Witty_ESP-12F2 = Gizwits WiFi Witty ESP-12F

nets:
  N1: Gizwits_WiFi_Witty_ESP-12F1.GPIO2, Gizwits_WiFi_Witty_ESP-12F2.GPIO16
  N2: Gizwits_WiFi_Witty_ESP-12F1.GPIO4, Gizwits_WiFi_Witty_ESP-12F2.GPIO14
